// Logisim project CalculoF.circ as structural Verilog: 1 circuit, main circuit CalculoF
module CalculoF (
  input  Clock,
  input  Reset,
  input  Start,
  input  [3:0] Y,
  input  [3:0] X,
  input  [3:0] A,
  input  [3:0] B,
  input  [3:0] C,
  output [15:0] ValorF
);

  wire Actualizar_Frow, CambiarFila, Primer_Paso;
  wire [15:0] A_16b, B_16b, C_16b, F_in_R, F_row_in_T, F_row_out, multiplexer_1_out, multiplexer_2_out,
       multiplexer_4_out, Salida;

  assign A_16b = {{12{A[3]}}, A};  // Bit_Extender bit_extender_1
  assign B_16b = {{12{B[3]}}, B};  // Bit_Extender bit_extender_2
  assign C_16b = {{12{C[3]}}, C};  // Bit_Extender bit_extender_3
  Multiplexer #(.width(16)) multiplexer_1 (.in0(ValorF), .in1(F_row_out), .out(multiplexer_1_out), .sel(CambiarFila));
  Multiplexer #(.width(16)) multiplexer_2 (.in0(A_16b), .in1(B_16b), .out(multiplexer_2_out), .sel(CambiarFila));
  Comparator #(.mode("unsigned"), .width(4)) comparator_1 (.a(X), .b(4'b1111), .eq(CambiarFila));  // open: gt, lt
  CarrySkipAdder carryskipadder_1 (.A(multiplexer_1_out), .B(multiplexer_2_out), .S(Salida));  // open: C_in, C_out
  D_Flip_Flop d_ff_1 (.D(1'b1), .clk(Clock), .Qn(Primer_Paso), .reset(Reset));  // open: Q, preset
  Multiplexer #(.width(16)) multiplexer_3 (.in0(Salida), .in1(C_16b), .out(F_in_R), .sel(Primer_Paso));
  Demultiplexer #(.width(16)) demultiplexer_1 (.out1(F_row_in_T), .in(F_in_R), .sel(Actualizar_Frow));  // open: out0
  or or_1 (Actualizar_Frow, CambiarFila, Primer_Paso);
  Register #(.width(16)) F (.D(F_in_R), .en(Start), .clk(Clock), .Q(ValorF), .clr(Reset));
  Register #(.width(16)) F_row (.D(multiplexer_4_out), .en(Start), .clk(Clock), .Q(F_row_out), .clr(Reset));
  Multiplexer #(.width(16)) multiplexer_4 (
    .in0(F_row_out), .in1(F_row_in_T), .out(multiplexer_4_out), .sel(Actualizar_Frow));

  // Other names for the same wires on the sheet: F_out[15:0] = ValorF
endmodule
