// Logisim project EvaluadorYRAM.circ as structural Verilog: 1 circuit, main circuit EvaluadorYRAM
module EvaluadorYRAM (
  input  [3:0] X,
  input  [3:0] Y,
  input  [15:0] F,
  input  Clock,
  input  Reset,
  input  Start,
  output [15:0] RAM_F,
  output RAM_LED
);

  wire d_ff_1_qn, LED_RAM_dout, MayorIgual;

  not not_1 (MayorIgual, F[15]);
  RAM #(.clearpin("true"), .dataWidth(16)) F_RAM (
    .addr({Y, X}), .we(Start), .oe(Start), .clk(Clock), .din(F), .dout(RAM_F), .clr(Reset));
  RAM #(.clearpin("true"), .dataWidth(1)) LED_RAM (
    .addr({Y, X}), .we(Start), .oe(Start), .clk(Clock), .din(MayorIgual), .dout(LED_RAM_dout), .clr(Reset));
  D_Flip_Flop d_ff_1 (.D(1'b1), .clk(Clock), .Qn(d_ff_1_qn), .reset(Reset));  // open: Q, preset
  Multiplexer multiplexer_1 (.in0(LED_RAM_dout), .in1(1'b0), .out(RAM_LED), .sel(d_ff_1_qn));

  // Other names for the same wires on the sheet: Address[7:0] = {Y, X}

  // Notes on the sheet:
  //   RAM_F
  //   RAM_LED
endmodule
