// Logisim project GeneradorPixeles.circ as structural Verilog: 1 circuit, main circuit GeneradorPixeles
module GeneradorPixeles (
  input  Reset,
  input  Clock,
  input  Start,
  output Fin,
  output [3:0] X,
  output [3:0] Y
);

  wire and_1_out, and_3_out, CarryX, CarryY, not_1_out, not_2_out;

  not not_1 (not_1_out, Fin);
  and and_1 (and_1_out, not_1_out, Start);
  contadorX contadorx_1 (.Reset(Reset), .Start(and_1_out), .Clock(Clock), .Carry(CarryX), .X(X));
  and and_2 (Fin, CarryX, CarryY);
  not not_2 (not_2_out, Fin);
  and and_3 (and_3_out, not_2_out, CarryX);
  contadorY contadory_1 (.Reset(Reset), .Start(and_3_out), .Clock(Clock), .Carry(CarryY), .Y(Y));
endmodule
