// Logisim project Rasterizador_grupo19.circ as structural Verilog: 2 circuits, main circuit main
module main (
  input  [3:0] A,
  input  [3:0] B,
  input  Start,
  input  Reset,
  input  Clock,
  input  [3:0] C,
  output Fin,
  output [15:0] RAM_F,
  output RAM_LED
);

  wire and_1_out, and_2_out, d_ff_1_qn, d_ff_2_qn, Fin_t, not_1_out, not_2_out, Start_D;
  wire [3:0] X, Y;
  wire [15:0] calculof_1_valorf, decoder_1_out0, demultiplexer_1_out1, demultiplexer_1_out2,
       demultiplexer_1_out3, demultiplexer_1_out4, demultiplexer_1_out5, demultiplexer_1_out6,
       demultiplexer_1_out7, demultiplexer_1_out8, demultiplexer_1_out9, demultiplexer_1_out10,
       demultiplexer_1_out11, demultiplexer_1_out12, demultiplexer_1_out13, demultiplexer_1_out14,
       demultiplexer_1_out15, OFFSET;

  not not_1 (not_1_out, Fin);
  and and_1 (and_1_out, not_1_out, Start);
  // GeneradorPixeles generadorpixeles_1: pin names not known; wires that end beside it: Start_D, Reset, Clock, Fin_t, Y, X
  // Probe on X
  CalculoF calculof_1 (
    .C(C), .A(A), .B(B), .Clock(Clock), .Enable(Start), .X(X), .Reset(Reset), .ValorF(calculof_1_valorf));
  EvaluadorYRAM evaluadoryram_1 (
    .Clock(Clock), .Enable(and_1_out), .F(calculof_1_valorf), .X(X), .Y(Y), .Reset(Reset), .RAM_F(RAM_F),
    .RAM_LED(RAM_LED));
  D_Flip_Flop d_ff_1 (.D(Fin_t), .clk(Clock), .Q(Fin), .Qn(d_ff_1_qn), .reset(Reset));  // open: preset
  D_Flip_Flop d_ff_2 (.D(Start), .clk(Clock), .Q(Start_D), .Qn(d_ff_2_qn), .reset(Reset));  // open: preset
  // NoConnect on d_ff_1_qn
  // NoConnect on d_ff_2_qn
  LED led_1 (.in(Fin));
  not not_2 (not_2_out, Clock);
  DotMatrix #(.matrixcols(16), .matrixrows(16), .persist(1000)) dotmatrix_1 (
    .col0(demultiplexer_1_out1), .col1(demultiplexer_1_out2), .col2(demultiplexer_1_out3),
    .col3(demultiplexer_1_out4), .col4(demultiplexer_1_out5), .col5(demultiplexer_1_out6),
    .col6(demultiplexer_1_out7), .col7(demultiplexer_1_out8), .col8(demultiplexer_1_out9),
    .col9(demultiplexer_1_out10), .col10(demultiplexer_1_out11), .col11(demultiplexer_1_out12),
    .col12(demultiplexer_1_out13), .col13(demultiplexer_1_out14), .col14(demultiplexer_1_out15),
    .col15(OFFSET));
  Demultiplexer #(.enable("true"), .select(4), .width(16)) demultiplexer_1 (
    .out0(OFFSET), .out1(demultiplexer_1_out1), .out2(demultiplexer_1_out2), .out3(demultiplexer_1_out3),
    .out4(demultiplexer_1_out4), .out5(demultiplexer_1_out5), .out6(demultiplexer_1_out6),
    .out7(demultiplexer_1_out7), .out8(demultiplexer_1_out8), .out9(demultiplexer_1_out9),
    .out10(demultiplexer_1_out10), .out11(demultiplexer_1_out11), .out12(demultiplexer_1_out12),
    .out13(demultiplexer_1_out13), .out14(demultiplexer_1_out14), .out15(demultiplexer_1_out15),
    .in(decoder_1_out0), .sel(X), .en(not_2_out));
  and and_2 (and_2_out, Start_D, RAM_LED);
  Decoder #(.select(4)) decoder_1 (
    .out0(decoder_1_out0[0]), .out1(decoder_1_out0[1]), .out2(decoder_1_out0[2]), .out3(decoder_1_out0[3]),
    .out4(decoder_1_out0[4]), .out5(decoder_1_out0[5]), .out6(decoder_1_out0[6]), .out7(decoder_1_out0[7]),
    .out8(decoder_1_out0[8]), .out9(decoder_1_out0[9]), .out10(decoder_1_out0[10]),
    .out11(decoder_1_out0[11]), .out12(decoder_1_out0[12]), .out13(decoder_1_out0[13]),
    .out14(decoder_1_out0[14]), .out15(decoder_1_out0[15]), .sel(Y), .en(and_2_out));

  // Other names for the same wires on the sheet: CortarRam = Fin; R_LED = RAM_LED

  // Notes on the sheet:
  //   El generador de pixeles requiere habilitarse
  //   1 pulso de reloj mas tarde que el resto
  //   La ram corta 1 pulso de reloj mas tarde que la señal de corte
  //   y aumentando el numero conforme sube
  //   entrada recibida con X como selector
  //   Habilitar la salida del DMUX en falling-edge
  //   actuales con el resultado de la coordenada anterior ya que
  //   por lo que habilitar solo en falling edge permite conocer
  //   los valores correctos para las coordenadas actuales
  //   Genera un numero de 16 bits con un 1 en la posicion equivalente a Y
  //   debido a la codificon de la altitud de la matriz led empezando con 0 abajo 
  //   Este DMUX determina a que columna pertenece la
  //   es necesario ya que si no, prende pixeles en las coordenadas 
  //   las coordenadas se actualizan mas rapido que el calculo del valor
endmodule

module testing (
  input  Start,
  input  Reset,
  input  [3:0] A,
  input  [3:0] B,
  input  [3:0] C
);

  wire clock_1_out, main_1_fin, main_1_ram_led;
  wire [15:0] main_1_ram_f;

  Clock clock_1 (.out(clock_1_out));
  // Probe on main_1_fin
  // Probe on main_1_ram_f
  main main_1 (
    .Clock(clock_1_out), .Start(Start), .A(A), .B(B), .C(C), .Reset(Reset), .RAM_F(main_1_ram_f),
    .RAM_LED(main_1_ram_led), .Fin(main_1_fin));
  // Probe on main_1_ram_led
endmodule
