// Logisim project contadorX.circ as structural Verilog: 1 circuit, main circuit contadorX
module contadorX (
  input  Reset,
  input  Start,
  input  Clock,
  output Carry,
  output [3:0] X
);

  Counter #(.max('hf), .trigger("falling"), .width(4)) counter_1 (
    .clr(Reset), .load(1'b0), .up(1'b1), .count(Start), .clk(Clock), .carry(Carry), .Q(X));  // open: D
endmodule
