// Logisim project contadorY.circ as structural Verilog: 1 circuit, main circuit contadorY
module contadorY (
  input  Reset,
  input  Start,
  input  Clock,
  output Carry,
  output [3:0] Y
);

  Counter #(.max('hf), .trigger("falling"), .width(4)) counter_1 (
    .clr(Reset), .load(1'b0), .up(1'b1), .count(Start), .clk(Clock), .carry(Carry), .Q(Y));  // open: D
endmodule
